// Logisim project Guia_1302.circ as structural Verilog: 1 circuit, main circuit main
module main (
);

  wire clock_1_out, j_k_ff_1_q, j_k_ff_2_q, j_k_ff_2_qn, j_k_ff_3_q, j_k_ff_3_qn, j_k_ff_4_q, j_k_ff_4_qn,
       j_k_ff_5_q, j_k_ff_5_qn, undriven, undriven_2, undriven_3, undriven_4;

  Clock clock_1 (.out(clock_1_out));
  J_K_Flip_Flop j_k_ff_1 (.J(clock_1_out), .clk(clock_1_out), .K(undriven), .Q(j_k_ff_1_q));  // open: Qn, preset, reset
  J_K_Flip_Flop j_k_ff_2 (
    .J(clock_1_out), .clk(j_k_ff_1_q), .K(undriven), .Q(j_k_ff_2_q), .Qn(j_k_ff_2_qn));  // open: preset, reset
  J_K_Flip_Flop j_k_ff_3 (
    .J(undriven_2), .clk(j_k_ff_2_q), .K(j_k_ff_2_qn), .Q(j_k_ff_3_q), .Qn(j_k_ff_3_qn));  // open: preset, reset
  J_K_Flip_Flop j_k_ff_4 (
    .J(undriven_3), .clk(j_k_ff_3_q), .K(j_k_ff_3_qn), .Q(j_k_ff_4_q), .Qn(j_k_ff_4_qn));  // open: preset, reset
  J_K_Flip_Flop j_k_ff_5 (
    .J(undriven_4), .clk(j_k_ff_4_q), .K(j_k_ff_4_qn), .Q(j_k_ff_5_q), .Qn(j_k_ff_5_qn));  // open: preset, reset
endmodule
