// Logisim project Guia_1304.circ as structural Verilog: 1 circuit, main circuit main
module main (
);

  wire clock_1_out, j_k_ff_1_q, j_k_ff_2_q, j_k_ff_3_q, j_k_ff_4_q, undriven;

  Clock clock_1 (.out(clock_1_out));
  J_K_Flip_Flop j_k_ff_1 (
    .J(clock_1_out), .clk(clock_1_out), .Q(j_k_ff_1_q), .reset(j_k_ff_4_q));  // open: K, Qn, preset
  J_K_Flip_Flop j_k_ff_2 (.J(j_k_ff_1_q), .Q(j_k_ff_2_q), .preset(j_k_ff_4_q));  // open: clk, K, Qn, reset
  J_K_Flip_Flop j_k_ff_3 (.J(j_k_ff_2_q), .Q(j_k_ff_3_q), .preset(undriven), .reset(undriven));  // open: clk, K, Qn
  J_K_Flip_Flop j_k_ff_4 (.J(j_k_ff_3_q), .Q(j_k_ff_4_q), .reset(undriven));  // open: clk, K, Qn, preset
endmodule
