// Logisim project Guia_1305.circ as structural Verilog: 1 circuit, main circuit main
module main (
);

  wire clock_1_out, t_ff_1_q, t_ff_2_q, t_ff_5_q, undriven;

  Clock clock_1 (.out(clock_1_out));
  T_Flip_Flop t_ff_1 (.clk(t_ff_5_q), .T(1'b1), .Q(t_ff_1_q), .preset(undriven));  // open: Qn, reset
  T_Flip_Flop t_ff_2 (.clk(t_ff_1_q), .T(t_ff_1_q), .Q(t_ff_2_q));  // open: Qn, preset, reset
  T_Flip_Flop t_ff_3 (.clk(t_ff_2_q), .T(t_ff_2_q), .Q(t_ff_1_q));  // open: Qn, preset, reset
  T_Flip_Flop t_ff_4 (.clk(t_ff_1_q), .T(t_ff_1_q));  // open: Q, Qn, preset, reset
  T_Flip_Flop t_ff_5 (.clk(clock_1_out), .T(undriven), .Q(t_ff_5_q));  // open: Qn, preset, reset
endmodule
