// Logisim project Questao02.circ as structural Verilog: 1 circuit, main circuit main
module main (
);

  wire and_1_out, not_1_out, not_2_out, or_1_out;

  // NOT_Gate not_1 has open pins: in=open, out=not_1_out
  // NOT_Gate not_2 has open pins: in=open, out=not_2_out
  buf or_1 (or_1_out, not_1_out);  // OR_Gate
  buf and_1 (and_1_out, not_2_out);  // AND_Gate
  // NAND_Gate nand_1 has open pins: in0=or_1_out, in1=and_1_out, out=open
endmodule
