// Logisim project questao03.circ as structural Verilog: 1 circuit, main circuit main
module main (
);

  wire and_1_out, multiplexer_1_out, multiplexer_2_out, not_1_out, not_2_out;

  // NOT_Gate not_1 has open pins: in=open, out=not_1_out
  // AND_Gate and_1 has open pins: out=and_1_out
  // NOT_Gate not_2 has open pins: in=open, out=not_2_out
  Multiplexer #(.enable("false")) multiplexer_1 (
    .in0(not_1_out), .in1(and_1_out), .out(multiplexer_1_out));  // open: sel
  Multiplexer #(.enable("false")) multiplexer_2 (
    .in0(and_1_out), .in1(not_2_out), .out(multiplexer_2_out));  // open: sel
  Multiplexer #(.enable("false")) multiplexer_3 (.in0(multiplexer_1_out), .in1(multiplexer_2_out));  // open: out, sel
endmodule
