// Logisim project questao05.circ as structural Verilog: 1 circuit, main circuit main
module main (
);

  wire nand_1_out, not_1_out, not_2_out, not_3_out, undriven, xnor_1_out;

  // NOT_Gate not_1 has open pins: in=open, out=not_1_out
  // NOT_Gate not_2 has open pins: in=open, out=not_2_out
  // NOT_Gate not_3 has open pins: in=open, out=not_3_out
  not xnor_1 (xnor_1_out, not_1_out);  // XNOR_Gate
  nand nand_1 (nand_1_out, not_2_out, not_3_out);
  // NAND_Gate nand_2 has open pins: in0=xnor_1_out, in1=undriven, out=open
  // NAND_Gate nand_3 has open pins: in0=undriven, in1=nand_1_out, out=open
endmodule
