// Logisim project Questao04.circ as structural Verilog: 1 circuit, main circuit main
module main (
);

  wire and_1_out, and_2_out, and_3_out, and_4_out, or_1_out, or_3_out, undriven, undriven_2, undriven_3,
       undriven_4, undriven_5, undriven_6, undriven_7, undriven_8, undriven_9, undriven_10, undriven_11,
       undriven_12;

  and and_1 (and_1_out, undriven, undriven_7);
  or or_1 (or_1_out, undriven_5, undriven_7);
  and and_2 (and_2_out, undriven_2, undriven_3);
  or or_2 (and_2_out, undriven_3, undriven_6);
  or or_3 (or_3_out, undriven_4, undriven_6);
  and and_3 (and_3_out, undriven_11, undriven_12);
  buf xor_1 (and_3_out, undriven_12);  // XOR_Gate
  and and_4 (and_4_out, undriven_8, undriven_10);
  or or_4 (and_4_out, undriven_9, undriven_10);

  // Notes on the sheet:
  //   a
  //   c
  //   c
  //   a
  //   c
  //   SbRb
  //   Da
  //   a
  //   c
  //   a
  //   c
  //   Tb
  //   Ta
endmodule
