// Logisim project Questao05a.circ as structural Verilog: 1 circuit, main circuit main
module main (
  input  in_1,
  output out_2
);

  wire d_ff_1_qn, d_ff_2_qn, d_ff_3_qn, d_ff_4_qn;

  Clock clock_1 (.out(in_1));
  D_Flip_Flop d_ff_1 (.clk(in_1), .Qn(d_ff_1_qn));  // open: D, Q, preset, reset
  D_Flip_Flop d_ff_2 (.clk(in_1), .D(d_ff_1_qn), .Qn(d_ff_2_qn));  // open: Q, preset, reset
  D_Flip_Flop d_ff_3 (.clk(in_1), .D(d_ff_2_qn), .Qn(d_ff_3_qn));  // open: Q, preset, reset
  D_Flip_Flop d_ff_4 (.clk(d_ff_3_qn), .D(in_1), .Qn(d_ff_4_qn));  // open: Q, preset, reset
  D_Flip_Flop d_ff_5 (.clk(d_ff_4_qn), .D(in_1), .Q(out_2));  // open: Qn, preset, reset
endmodule
