// Logisim project questao02.circ as structural Verilog: 1 circuit, main circuit main
module main (
);

  wire and_1_out, and_2_out, and_4_out, and_5_out, and_6_out, and_8_out, and_9_out, multiplexer_1_out,
       nand_1_out, nand_2_out, nand_3_out, not_1_out, not_2_out, undriven, undriven_2, undriven_3,
       undriven_4, undriven_5, undriven_6, undriven_7, undriven_8, undriven_9, undriven_10, undriven_11,
       undriven_12;

  not not_1 (not_1_out, undriven_2);
  not not_2 (not_2_out, undriven_3);
  and and_1 (and_1_out, undriven_5, undriven_11);
  and and_2 (and_2_out, undriven_6, undriven_11);
  and and_3 (and_2_out, undriven_11, undriven_7);
  and and_4 (and_4_out, undriven_8, undriven_12);
  and and_5 (and_5_out, undriven_12, undriven_9);
  and and_6 (and_6_out, undriven, not_1_out);
  // AND_Gate and_7 has open pins: in1=undriven_10, out=open
  not nand_1 (nand_1_out, undriven_3);  // NAND_Gate
  Multiplexer #(.enable("false")) multiplexer_1 (.out(multiplexer_1_out));  // open: in0, in1, sel
  not nand_2 (nand_2_out, undriven_4);  // NAND_Gate
  and and_8 (and_8_out, and_1_out, and_2_out);
  and and_9 (and_9_out, and_4_out, and_5_out);
  buf and_10 (and_9_out, and_5_out);  // AND_Gate
  nand nand_3 (nand_3_out, nand_1_out, multiplexer_1_out);
  nand nand_4 (nand_3_out, multiplexer_1_out, nand_2_out);

  // Notes on the sheet:
  //   a
  //   b
  //   c
  //   a
  //   b
  //   c
  //   a
  //   b
  //   c
  //   a
  //   b
  //   c
endmodule
