// Logisim project Questao03.circ as structural Verilog: 1 circuit, main circuit main
module main (
);

  wire clock_1_out, j_k_ff_1_q, j_k_ff_2_q, undriven;

  Clock clock_1 (.out(clock_1_out));
  J_K_Flip_Flop j_k_ff_1 (.J(clock_1_out), .Q(j_k_ff_1_q));  // open: clk, K, Qn, preset, reset
  J_K_Flip_Flop j_k_ff_2 (.clk(j_k_ff_1_q), .K(undriven), .Q(j_k_ff_2_q));  // open: J, Qn, preset, reset
  J_K_Flip_Flop j_k_ff_3 (.clk(j_k_ff_2_q), .K(undriven));  // open: J, Q, Qn, preset, reset
endmodule
