// Logisim project Guia_1303.circ as structural Verilog: 1 circuit, main circuit main
module main (
);

  wire clock_1_out, j_k_ff_1_q, j_k_ff_2_q, j_k_ff_3_q, j_k_ff_4_q, j_k_ff_5_q, j_k_ff_5_qn;

  Clock clock_1 (.out(clock_1_out));
  J_K_Flip_Flop j_k_ff_1 (.J(clock_1_out), .clk(j_k_ff_5_q), .K(1'b1), .Q(j_k_ff_1_q));  // open: Qn, preset, reset
  J_K_Flip_Flop j_k_ff_2 (.clk(j_k_ff_1_q), .K(1'b1), .Q(j_k_ff_2_q));  // open: J, Qn, preset, reset
  J_K_Flip_Flop j_k_ff_3 (.clk(j_k_ff_2_q), .K(1'b1), .Q(j_k_ff_3_q));  // open: J, Qn, preset, reset
  J_K_Flip_Flop j_k_ff_4 (.clk(j_k_ff_3_q), .K(1'b1), .Q(j_k_ff_4_q));  // open: J, Qn, preset, reset
  J_K_Flip_Flop j_k_ff_5 (.clk(j_k_ff_4_q), .K(1'b1), .Q(j_k_ff_5_q), .Qn(j_k_ff_5_qn));  // open: J, preset, reset
endmodule
