// Logisim project Questao04.circ as structural Verilog: 1 circuit, main circuit main
module main (
  input  in_1
);

  wire clock_1_out, t_ff_1_qn, t_ff_2_qn, t_ff_3_q;

  Clock clock_1 (.out(clock_1_out));
  T_Flip_Flop t_ff_1 (.T(clock_1_out), .Qn(t_ff_1_qn), .preset(in_1));  // open: clk, Q, reset
  T_Flip_Flop t_ff_2 (.T(t_ff_1_qn), .Qn(t_ff_2_qn), .preset(in_1));  // open: clk, Q, reset
  T_Flip_Flop t_ff_3 (.T(t_ff_2_qn), .Q(t_ff_3_q), .preset(in_1));  // open: clk, Qn, reset

  // Notes on the sheet:
  //   Q3
endmodule
