// Logisim project Questao05b.circ as structural Verilog: 1 circuit, main circuit main
module main (
  input  in_1
);

  wire clock_1_out;

  Clock clock_1 (.out(clock_1_out));
  D_Flip_Flop d_ff_1 (.clk(clock_1_out), .Q(clock_1_out), .preset(in_1));  // open: D, Qn, reset
  D_Flip_Flop d_ff_2 (.clk(clock_1_out), .Q(clock_1_out));  // open: D, Qn, preset, reset
  D_Flip_Flop d_ff_3 (.clk(clock_1_out), .Q(clock_1_out));  // open: D, Qn, preset, reset
  D_Flip_Flop d_ff_4 (.clk(clock_1_out), .Q(in_1));  // open: D, Qn, preset, reset
endmodule
