// Logisim project questao03.circ as structural Verilog: 1 circuit, main circuit main
module main (
);

  wire not_1_out, not_2_out, undriven, undriven_2;

  not not_1 (not_1_out, undriven);
  not not_2 (not_2_out, undriven_2);
  not not_3 (not_2_out, undriven_2);
  // OR_Gate or_1 has open pins: in0=not_1_out, in1=not_2_out, out=open

  // Notes on the sheet:
  //   a
  //   b
  //   c
endmodule
