// Logisim project Questao05.circ as structural Verilog: 1 circuit, main circuit main
module main (
);

  wire clock_1_out, j_k_ff_1_q, j_k_ff_1_qn, j_k_ff_2_q, j_k_ff_2_qn;

  Clock clock_1 (.out(clock_1_out));
  J_K_Flip_Flop j_k_ff_1 (.clk(clock_1_out), .Q(j_k_ff_1_q), .Qn(j_k_ff_1_qn));  // open: J, K, preset, reset
  J_K_Flip_Flop j_k_ff_2 (
    .J(j_k_ff_1_qn), .clk(j_k_ff_1_q), .Q(j_k_ff_2_q), .Qn(j_k_ff_2_qn));  // open: K, preset, reset
  J_K_Flip_Flop j_k_ff_3 (.J(j_k_ff_2_qn), .clk(j_k_ff_2_q));  // open: K, Q, Qn, preset, reset
endmodule
