// Logisim project Questao06.circ as structural Verilog: 1 circuit, main circuit main
module main (
);

  wire clock_1_out, j_k_ff_1_q, j_k_ff_2_q, j_k_ff_3_q, undriven;

  Clock clock_1 (.out(clock_1_out));
  J_K_Flip_Flop j_k_ff_1 (.J(clock_1_out), .K(undriven), .Q(j_k_ff_1_q));  // open: clk, Qn, preset, reset
  J_K_Flip_Flop j_k_ff_2 (.J(j_k_ff_1_q), .K(undriven), .Q(j_k_ff_2_q));  // open: clk, Qn, preset, reset
  J_K_Flip_Flop j_k_ff_3 (.J(j_k_ff_2_q), .K(undriven), .Q(j_k_ff_3_q));  // open: clk, Qn, preset, reset

  // Notes on the sheet:
  //   Q3
endmodule
